# Fritzing sketch intro_potentiometer_led (saved by Fritzing 0.9.3b)
breadboards: 1

parts:
  Part1 = Arduino Uno (Rev3)
  R1 = Rotary Potentiometer (Small) [maximum_resistance=100kΩ package=THT]
  LED2 = LED - 5mm [color="Green (560nm)" package="5 mm [THT]"]
  LED1 = smd LED [color="Red (633nm)" package="0805 [SMD]"]
  LED3 = LED - 5mm [color="Yellow (595nm)" package="5 mm [THT]"]  # not connected
  R2 = Resistor [tolerance=±5% resistance=220 package=THT]  # not connected
  R3 = Resistor [tolerance=±5% resistance=220 package=THT]
  R4 = Resistor [tolerance=±5% resistance=220 package=THT]

nets:
  N1: Part1.A0, R1.wiper
  N2: Part1.D3_PWM, R3.Pin_0
  N3: Part1.D4, R4.Pin_0
  N4: Part1.5V, R1.leg2
  N5: Part1.GND, R1.leg1, LED2.cathode, LED1.cathode
  N6: LED2.anode, R4.Pin_1
