# Fritzing sketch RGB_LED_buttons (saved by Fritzing 0.9.3b)
breadboards: 1

parts:
  LED1 = RGB LED (com. cathode, rgb) [package="5 mm [THT]"]
  Part1 = Arduino Uno (Rev3)
  R1 = Resistor [tolerance=±5% resistance=1k package=THT]
  R2 = Resistor [tolerance=±5% resistance=1k package=THT]
  R3 = Resistor [tolerance=±5% resistance=1k package=THT]
  S1 = Pushbutton [package="[THT]"]
  S2 = Pushbutton [package="[THT]"]
  S3 = Pushbutton [package="[THT]"]
  R4 = Resistor [tolerance=±5% resistance=1k package=THT]
  R5 = Resistor [tolerance=±5% resistance=1k package=THT]
  R6 = Resistor [tolerance=±5% resistance=1k package=THT]

nets:
  N1: LED1.red_anode, R1.Pin_1
  N2: LED1.green_anode, R2.Pin_1
  N3: LED1.blue_anode, R3.Pin_1
  N4: Part1.D10_PWM/SS, R3.Pin_0
  N5: Part1.D11_PWM/MOSI, R2.Pin_0
  N6: Part1.D13/SCK, R1.Pin_0
  N7: Part1.GND, R4.Pin_1, R5.Pin_1, R6.Pin_1
  N8: Part1.D5_PWM, S3.Pin_1, S3.Pin_2, R6.Pin_0
  N9: Part1.D6_PWM, S2.Pin_1, S2.Pin_2, R5.Pin_0
  N10: Part1.D7, S1.Pin_1, S1.Pin_2, R4.Pin_0
  N11: Part1.5V, S1.Pin_3, S1.Pin_4, S2.Pin_3, S2.Pin_4, S3.Pin_3, S3.Pin_4
