# Fritzing sketch Active_buzzer (saved by Fritzing 0.9.3b)
breadboards: 1

parts:
  Part1 = Arduino Uno (Rev3)
  J1 = Piezo Speaker
  S1 = Pushbutton [package="[SMD]"]
  R1 = Resistor [tolerance=±5% resistance=1k package=THT]
  R2 = Resistor [tolerance=±5% resistance=220 package=THT]

nets:
  N1: Part1.D12/MISO, S1.Pin_3, S1.Pin_4, R1.Pin_0
  N2: Part1.D13/SCK, J1.pin2
  N3: Part1.5V, S1.Pin_1, S1.Pin_2
  N4: Part1.GND, R1.Pin_1, R2.Pin_0
  N5: J1.pin1, R2.Pin_1
